// Logisim project circuit_4.circ as structural Verilog: 1 circuit, main circuit main
module main (
);

  wire D_1_2_out, D_1_3_out, D_1_4_out, D_1_5_out, D_1_6_out, D_1_7_out, D_1_out, or_1_out, or_2_out,
       or_3_out, or_4_out, or_5_out, or_6_out, or_7_out, undriven, undriven_2, undriven_3;

  not D_1 (D_1_out, undriven);
  not D_1_2 (D_1_2_out, undriven_2);
  not D_1_3 (D_1_3_out, undriven_3);
  or or_1 (or_1_out, D_1_out, undriven_2, undriven_3);
  or or_2 (or_2_out, D_1_out, D_1_2_out, D_1_3_out);
  or or_3 (or_3_out, D_1_out, undriven_2, undriven_3);
  or or_4 (or_4_out, D_1_out, undriven_2, D_1_3_out);
  or or_5 (or_5_out, undriven, D_1_2_out, D_1_3_out);
  not D_1_4 (D_1_4_out, or_2_out);
  not D_1_5 (D_1_5_out, or_3_out);
  not D_1_6 (D_1_6_out, or_4_out);
  not D_1_7 (D_1_7_out, or_5_out);
  or or_6 (or_6_out, D_1_4_out, D_1_5_out);
  or or_7 (or_7_out, D_1_6_out, D_1_7_out);

  // Notes on the sheet:
  //   A_0
  //   A_1
  //   A_2
  //   Y_0
  //   Y_1
  //   Y_2
  //   Y_3
endmodule
